// Logisim project CPU.circ as structural Verilog: 14 circuits, main circuit CPU
module Register_File (
  input  [3:0] dr,
  input  Write_Enable,
  input  [17:0] inData,
  input  clk,
  input  [3:0] sr1,
  input  [3:0] sr2,
  output [17:0] outdata1,
  output [17:0] outdata2,
  output [17:0] out_9,
  output [17:0] out_10,
  output [17:0] out_11,
  output [17:0] out_12,
  output [17:0] out_13,
  output [17:0] out_14,
  output [17:0] out_15,
  output [17:0] out_16,
  output [17:0] out_17,
  output [17:0] out_18,
  output [17:0] out_19,
  output [17:0] out_20,
  output [17:0] out_21,
  output [17:0] out_22,
  output [17:0] out_23,
  output [17:0] out_24
);

  wire and_1_out, and_2_out, and_3_out, and_4_out, and_5_out, and_6_out, and_7_out, and_8_out, and_9_out,
       and_10_out, and_11_out, and_12_out, and_13_out, and_14_out, and_15_out, and_16_out, decoder_1_out0,
       decoder_1_out1, decoder_1_out2, decoder_1_out3, decoder_1_out4, decoder_1_out5, decoder_1_out6,
       decoder_1_out7, decoder_1_out8, decoder_1_out9, decoder_1_out10, decoder_1_out11, decoder_1_out12,
       decoder_1_out13, decoder_1_out14, decoder_1_out15, decoder_2_out0, decoder_2_out1, decoder_2_out2,
       decoder_2_out3, decoder_2_out4, decoder_2_out5, decoder_2_out6, decoder_2_out7, decoder_2_out8,
       decoder_2_out9, decoder_2_out10, decoder_2_out11, decoder_2_out12, decoder_2_out13, decoder_2_out14,
       decoder_2_out15, decoder_3_out0, decoder_3_out1, decoder_3_out2, decoder_3_out3, decoder_3_out4,
       decoder_3_out5, decoder_3_out6, decoder_3_out7, decoder_3_out8, decoder_3_out9, decoder_3_out10,
       decoder_3_out11, decoder_3_out12, decoder_3_out13, decoder_3_out14, decoder_3_out15;

  Decoder #(.select(4), .enable("false")) decoder_1 (
    .out0(decoder_1_out0), .out1(decoder_1_out1), .out2(decoder_1_out2), .out3(decoder_1_out3),
    .out4(decoder_1_out4), .out5(decoder_1_out5), .out6(decoder_1_out6), .out7(decoder_1_out7),
    .out8(decoder_1_out8), .out9(decoder_1_out9), .out10(decoder_1_out10), .out11(decoder_1_out11),
    .out12(decoder_1_out12), .out13(decoder_1_out13), .out14(decoder_1_out14), .out15(decoder_1_out15),
    .sel(dr));
  and and_1 (and_1_out, decoder_1_out0, Write_Enable);
  and and_2 (and_2_out, decoder_1_out1, Write_Enable);
  and and_3 (and_3_out, decoder_1_out2, Write_Enable);
  and and_4 (and_4_out, decoder_1_out3, Write_Enable);
  and and_5 (and_5_out, decoder_1_out4, Write_Enable);
  and and_6 (and_6_out, decoder_1_out5, Write_Enable);
  and and_7 (and_7_out, decoder_1_out6, Write_Enable);
  and and_8 (and_8_out, decoder_1_out7, Write_Enable);
  and and_9 (and_9_out, decoder_1_out8, Write_Enable);
  and and_10 (and_10_out, decoder_1_out9, Write_Enable);
  and and_11 (and_11_out, decoder_1_out10, Write_Enable);
  and and_12 (and_12_out, decoder_1_out11, Write_Enable);
  and and_13 (and_13_out, decoder_1_out12, Write_Enable);
  and and_14 (and_14_out, decoder_1_out13, Write_Enable);
  and and_15 (and_15_out, decoder_1_out14, Write_Enable);
  and and_16 (and_16_out, decoder_1_out15, Write_Enable);
  Register #(.width(18)) register_1 (.D(inData), .en(and_1_out), .Q(out_9), .clk(clk), .clr(1'b0));
  Register #(.width(18)) register_2 (.D(inData), .en(and_2_out), .Q(out_10), .clk(clk), .clr(1'b0));
  Register #(.width(18)) register_3 (.D(inData), .en(and_3_out), .Q(out_11), .clk(clk), .clr(1'b0));
  Register #(.width(18)) register_4 (.D(inData), .en(and_4_out), .Q(out_12), .clk(clk), .clr(1'b0));
  Register #(.width(18)) register_5 (.D(inData), .en(and_5_out), .Q(out_13), .clk(clk), .clr(1'b0));
  Register #(.width(18)) register_6 (.D(inData), .en(and_6_out), .Q(out_14), .clk(clk), .clr(1'b0));
  Register #(.width(18)) register_7 (.D(inData), .en(and_7_out), .Q(out_15), .clk(clk), .clr(1'b0));
  Register #(.width(18)) register_8 (.D(inData), .en(and_8_out), .Q(out_16), .clk(clk), .clr(1'b0));
  Register #(.width(18)) register_9 (.D(inData), .en(and_9_out), .Q(out_17), .clk(clk), .clr(1'b0));
  Register #(.width(18)) register_10 (.D(inData), .en(and_10_out), .Q(out_18), .clk(clk), .clr(1'b0));
  Register #(.width(18)) register_11 (.D(inData), .en(and_11_out), .Q(out_19), .clk(clk), .clr(1'b0));
  Register #(.width(18)) register_12 (.D(inData), .en(and_12_out), .Q(out_20), .clk(clk), .clr(1'b0));
  Register #(.width(18)) register_13 (.D(inData), .en(and_13_out), .Q(out_21), .clk(clk), .clr(1'b0));
  Register #(.width(18)) register_14 (.D(inData), .en(and_14_out), .Q(out_22), .clk(clk), .clr(1'b0));
  Register #(.width(18)) register_15 (.D(inData), .en(and_15_out), .Q(out_23), .clk(clk), .clr(1'b0));
  Register #(.width(18)) register_16 (.D(inData), .en(and_16_out), .Q(out_24), .clk(clk), .clr(1'b0));
  Decoder #(.select(4), .enable("false")) decoder_2 (
    .out0(decoder_2_out0), .out1(decoder_2_out1), .out2(decoder_2_out2), .out3(decoder_2_out3),
    .out4(decoder_2_out4), .out5(decoder_2_out5), .out6(decoder_2_out6), .out7(decoder_2_out7),
    .out8(decoder_2_out8), .out9(decoder_2_out9), .out10(decoder_2_out10), .out11(decoder_2_out11),
    .out12(decoder_2_out12), .out13(decoder_2_out13), .out14(decoder_2_out14), .out15(decoder_2_out15),
    .sel(sr1));
  Decoder #(.select(4), .enable("false")) decoder_3 (
    .out0(decoder_3_out0), .out1(decoder_3_out1), .out2(decoder_3_out2), .out3(decoder_3_out3),
    .out4(decoder_3_out4), .out5(decoder_3_out5), .out6(decoder_3_out6), .out7(decoder_3_out7),
    .out8(decoder_3_out8), .out9(decoder_3_out9), .out10(decoder_3_out10), .out11(decoder_3_out11),
    .out12(decoder_3_out12), .out13(decoder_3_out13), .out14(decoder_3_out14), .out15(decoder_3_out15),
    .sel(sr2));
  assign outdata1 = decoder_2_out0 ? out_9 : 18'bz;  // Controlled_Buffer controlled_buffer_1
  assign outdata2 = decoder_3_out0 ? out_9 : 18'bz;  // Controlled_Buffer controlled_buffer_2
  assign outdata1 = decoder_2_out1 ? out_10 : 18'bz;  // Controlled_Buffer controlled_buffer_3
  assign outdata2 = decoder_3_out1 ? out_10 : 18'bz;  // Controlled_Buffer controlled_buffer_4
  assign outdata1 = decoder_2_out2 ? out_11 : 18'bz;  // Controlled_Buffer controlled_buffer_5
  assign outdata2 = decoder_3_out2 ? out_11 : 18'bz;  // Controlled_Buffer controlled_buffer_6
  assign outdata1 = decoder_2_out3 ? out_12 : 18'bz;  // Controlled_Buffer controlled_buffer_7
  assign outdata2 = decoder_3_out3 ? out_12 : 18'bz;  // Controlled_Buffer controlled_buffer_8
  assign outdata1 = decoder_2_out4 ? out_13 : 18'bz;  // Controlled_Buffer controlled_buffer_9
  assign outdata2 = decoder_3_out4 ? out_13 : 18'bz;  // Controlled_Buffer controlled_buffer_10
  assign outdata1 = decoder_2_out5 ? out_14 : 18'bz;  // Controlled_Buffer controlled_buffer_11
  assign outdata2 = decoder_3_out5 ? out_14 : 18'bz;  // Controlled_Buffer controlled_buffer_12
  assign outdata1 = decoder_2_out6 ? out_15 : 18'bz;  // Controlled_Buffer controlled_buffer_13
  assign outdata2 = decoder_3_out6 ? out_15 : 18'bz;  // Controlled_Buffer controlled_buffer_14
  assign outdata1 = decoder_2_out7 ? out_16 : 18'bz;  // Controlled_Buffer controlled_buffer_15
  assign outdata2 = decoder_3_out7 ? out_16 : 18'bz;  // Controlled_Buffer controlled_buffer_16
  assign outdata1 = decoder_2_out8 ? out_17 : 18'bz;  // Controlled_Buffer controlled_buffer_17
  assign outdata2 = decoder_3_out8 ? out_17 : 18'bz;  // Controlled_Buffer controlled_buffer_18
  assign outdata1 = decoder_2_out9 ? out_18 : 18'bz;  // Controlled_Buffer controlled_buffer_19
  assign outdata2 = decoder_3_out9 ? out_18 : 18'bz;  // Controlled_Buffer controlled_buffer_20
  assign outdata1 = decoder_2_out10 ? out_19 : 18'bz;  // Controlled_Buffer controlled_buffer_21
  assign outdata2 = decoder_3_out10 ? out_19 : 18'bz;  // Controlled_Buffer controlled_buffer_22
  assign outdata1 = decoder_2_out11 ? out_20 : 18'bz;  // Controlled_Buffer controlled_buffer_23
  assign outdata2 = decoder_3_out11 ? out_20 : 18'bz;  // Controlled_Buffer controlled_buffer_24
  assign outdata1 = decoder_2_out12 ? out_21 : 18'bz;  // Controlled_Buffer controlled_buffer_25
  assign outdata2 = decoder_3_out12 ? out_21 : 18'bz;  // Controlled_Buffer controlled_buffer_26
  assign outdata1 = decoder_2_out13 ? out_22 : 18'bz;  // Controlled_Buffer controlled_buffer_27
  assign outdata2 = decoder_3_out13 ? out_22 : 18'bz;  // Controlled_Buffer controlled_buffer_28
  assign outdata1 = decoder_2_out14 ? out_23 : 18'bz;  // Controlled_Buffer controlled_buffer_29
  assign outdata2 = decoder_3_out14 ? out_23 : 18'bz;  // Controlled_Buffer controlled_buffer_30
  assign outdata1 = decoder_2_out15 ? out_24 : 18'bz;  // Controlled_Buffer controlled_buffer_31
  assign outdata2 = decoder_3_out15 ? out_24 : 18'bz;  // Controlled_Buffer controlled_buffer_32

  // Other names for the same wires on the sheet: R0[17:0] = out_9; R1[17:0] = out_10; R2[17:0] = out_11;
  //   R3[17:0] = out_12; R4[17:0] = out_13; R5[17:0] = out_14; R6[17:0] = out_15; R7[17:0] = out_16;
  //   R8[17:0] = out_17; R9[17:0] = out_18; R10[17:0] = out_19; R11[17:0] = out_20; R12[17:0] = out_21;
  //   R13[17:0] = out_22; R14[17:0] = out_23; R15[17:0] = out_24
endmodule

module Arithmetic_Logic_Unit (
  input  imm_or_register,
  input  [1:0] in_2,
  input  [17:0] input1,
  input  [17:0] input2,
  input  [5:0] immediate_value,
  output [17:0] sum
);

  wire not_1_out, not_2_out, not_3_out;
  wire [17:0] and_1_out, bit_extender_1_out, controlled_buffer_1_out, controlled_buffer_3_out,
       controlled_buffer_6_out, controlled_buffer_7_out, controlled_buffer_9_out, n18_bit_adder_1_output,
       or_1_out, xor_1_out;

  not not_1 (not_1_out, imm_or_register);
  assign bit_extender_1_out = {{12{1'b0}}, immediate_value};  // Bit_Extender bit_extender_1
  assign controlled_buffer_1_out = not_1_out ? input2 : 18'bz;  // Controlled_Buffer controlled_buffer_1
  assign controlled_buffer_1_out = imm_or_register ? bit_extender_1_out : 18'bz;  // Controlled_Buffer controlled_buffer_2
  _18_bit_Adder u_18_bit_adder_1 (.input1(input1), .input2(controlled_buffer_1_out), .\output (n18_bit_adder_1_output));
  assign and_1_out = input1 & controlled_buffer_1_out;  // AND_Gate and_1, 18 bits wide
  assign or_1_out = input1 | controlled_buffer_1_out;  // OR_Gate or_1, 18 bits wide
  assign xor_1_out = input1 ^ controlled_buffer_1_out;  // XOR_Gate xor_1, 18 bits wide
  not not_2 (not_2_out, in_2[1]);
  not not_3 (not_3_out, in_2[0]);
  assign controlled_buffer_3_out = not_2_out ? n18_bit_adder_1_output : 18'bz;  // Controlled_Buffer controlled_buffer_3
  assign sum = in_2[0] ? controlled_buffer_3_out : 18'bz;  // Controlled_Buffer controlled_buffer_4
  assign sum = not_3_out ? controlled_buffer_6_out : 18'bz;  // Controlled_Buffer controlled_buffer_5
  assign controlled_buffer_6_out = not_2_out ? and_1_out : 18'bz;  // Controlled_Buffer controlled_buffer_6
  assign controlled_buffer_7_out = in_2[1] ? or_1_out : 18'bz;  // Controlled_Buffer controlled_buffer_7
  assign sum = not_3_out ? controlled_buffer_7_out : 18'bz;  // Controlled_Buffer controlled_buffer_8
  assign controlled_buffer_9_out = in_2[1] ? xor_1_out : 18'bz;  // Controlled_Buffer controlled_buffer_9
  assign sum = in_2[0] ? controlled_buffer_9_out : 18'bz;  // Controlled_Buffer controlled_buffer_10
endmodule

module _18_bit_Adder (
  input  [17:0] input1,
  input  [17:0] input2,
  output [17:0] \output 
);

  wire full_adder_1_cout, full_adder_2_cout, full_adder_3_cout, full_adder_4_cout, full_adder_5_cout,
       full_adder_6_cout, full_adder_7_cout, full_adder_8_cout, full_adder_9_cout, full_adder_10_cout,
       full_adder_11_cout, full_adder_12_cout, full_adder_13_cout, full_adder_14_cout, full_adder_15_cout,
       full_adder_16_cout, full_adder_17_cout, full_adder_18_cout;

  Full_adder full_adder_1 (.a(input2[0]), .b(input1[0]), .cin(1'b0), .s(\output [0]), .cout(full_adder_1_cout));
  Full_adder full_adder_2 (
    .a(input2[9]), .b(input1[9]), .cin(full_adder_17_cout), .s(\output [9]), .cout(full_adder_2_cout));
  Full_adder full_adder_3 (
    .a(input1[1]), .b(input2[1]), .cin(full_adder_1_cout), .s(\output [1]), .cout(full_adder_3_cout));
  Full_adder full_adder_4 (
    .a(input2[10]), .b(input1[10]), .cin(full_adder_2_cout), .s(\output [10]), .cout(full_adder_4_cout));
  Full_adder full_adder_5 (
    .a(input1[2]), .b(input2[2]), .cin(full_adder_3_cout), .s(\output [2]), .cout(full_adder_5_cout));
  Full_adder full_adder_6 (
    .a(input2[11]), .b(input1[11]), .cin(full_adder_4_cout), .s(\output [11]), .cout(full_adder_6_cout));
  Full_adder full_adder_7 (
    .a(input1[3]), .b(input2[3]), .cin(full_adder_5_cout), .s(\output [3]), .cout(full_adder_7_cout));
  Full_adder full_adder_8 (
    .a(input2[12]), .b(input1[12]), .cin(full_adder_6_cout), .s(\output [12]), .cout(full_adder_8_cout));
  Full_adder full_adder_9 (
    .a(input1[4]), .b(input2[4]), .cin(full_adder_7_cout), .s(\output [4]), .cout(full_adder_9_cout));
  Full_adder full_adder_10 (
    .a(input2[13]), .b(input1[13]), .cin(full_adder_8_cout), .s(\output [13]), .cout(full_adder_10_cout));
  Full_adder full_adder_11 (
    .a(input1[5]), .b(input2[5]), .cin(full_adder_9_cout), .s(\output [5]), .cout(full_adder_11_cout));
  Full_adder full_adder_12 (
    .a(input2[14]), .b(input1[14]), .cin(full_adder_10_cout), .s(\output [14]), .cout(full_adder_12_cout));
  Full_adder full_adder_13 (
    .a(input1[6]), .b(input2[6]), .cin(full_adder_11_cout), .s(\output [6]), .cout(full_adder_13_cout));
  Full_adder full_adder_14 (
    .a(input2[15]), .b(input1[15]), .cin(full_adder_12_cout), .s(\output [15]), .cout(full_adder_14_cout));
  Full_adder full_adder_15 (
    .a(input1[7]), .b(input2[7]), .cin(full_adder_13_cout), .s(\output [7]), .cout(full_adder_15_cout));
  Full_adder full_adder_16 (
    .a(input2[16]), .b(input1[16]), .cin(full_adder_14_cout), .s(\output [16]), .cout(full_adder_16_cout));
  Full_adder full_adder_17 (
    .a(input1[8]), .b(input2[8]), .cin(full_adder_15_cout), .s(\output [8]), .cout(full_adder_17_cout));
  Full_adder full_adder_18 (
    .a(input2[17]), .b(input1[17]), .cin(full_adder_16_cout), .s(\output [17]), .cout(full_adder_18_cout));
endmodule

// ControlUnit
module Control_Unit (
  input  [17:0] in_1,
  input  clk,
  output [17:0] out_3,
  output is_ALU,
  output [1:0] alu_operate_code_2bit,
  output immediate,
  output memread,
  output memwrite,
  output write_enable,
  output pcwrite,
  output [3:0] dest,
  output [3:0] source1,
  output [3:0] source2,
  output JUMP,
  output is_Branch
);

  wire and_1_out, and_2_out, decoder_1_out1, decoder_1_out2, decoder_1_out3, decoder_1_out4, decoder_1_out5,
       decoder_1_out6, decoder_1_out7, decoder_1_out8, decoder_1_out11, decoder_1_out12, decoder_1_out13,
       decoder_1_out14, decoder_1_out15, fetch1, not_1_out, not_2_out, not_3_out, not_4_out, not_5_out,
       or_1_out, register_1_q;
  wire [1:0] alu_control_immediate_out_5;
  wire [3:0] counter_1_q;

  assign source1 = and_1_out ? in_1[13:10] : 4'bz;  // Controlled_Buffer controlled_buffer_1
  assign source1 = not_1_out ? in_1[9:6] : 4'bz;  // Controlled_Buffer controlled_buffer_2
  not not_1 (not_1_out, and_1_out);
  Decoder #(.select(4), .enable("false")) decoder_1 (
    .out0(fetch1), .out1(decoder_1_out1), .out2(decoder_1_out2), .out3(decoder_1_out3),
    .out4(decoder_1_out4), .out5(decoder_1_out5), .out6(decoder_1_out6), .out7(decoder_1_out7),
    .out8(decoder_1_out8), .out9(memwrite), .out10(JUMP), .out11(decoder_1_out11), .out12(decoder_1_out12),
    .out13(decoder_1_out13), .out14(decoder_1_out14), .out15(decoder_1_out15), .sel(counter_1_q));
  not not_2 (not_2_out, in_1[15]);
  not not_3 (not_3_out, in_1[16]);
  and and_1 (and_1_out, in_1[17], not_3_out, not_2_out, in_1[14]);
  Counter #(.width(4), .max('hf), .ongoal("load")) counter_1 (
    .load(decoder_1_out1), .D(in_1[17:14]), .count(or_1_out), .Q(counter_1_q), .clk(clk), .clr(and_2_out));  // open: carry
  and and_2 (and_2_out, not_4_out, register_1_q);
  not not_4 (not_4_out, or_1_out);
  Register #(.width(1)) register_1 (.D(pcwrite), .en(1'b1), .Q(register_1_q), .clk(clk), .clr(1'b0));
  or or_1 (or_1_out, fetch1, decoder_1_out7);
  assign alu_operate_code_2bit = decoder_1_out2 ? in_1[1:0] : 2'bz;  // Controlled_Buffer controlled_buffer_3
  ALU_Immediate_Control alu_control_immediate (
    .addi(decoder_1_out3), .ori(decoder_1_out5), .xori(decoder_1_out6),
    .out_4(alu_control_immediate_out_5[1]), .out_5(alu_control_immediate_out_5[0]));
  or or_2 (is_Branch, decoder_1_out11, decoder_1_out12, decoder_1_out13, decoder_1_out14, decoder_1_out15);
  not not_5 (not_5_out, decoder_1_out2);
  or or_3 (immediate, decoder_1_out4, decoder_1_out3, decoder_1_out5, decoder_1_out6);
  assign alu_operate_code_2bit = not_5_out ? alu_control_immediate_out_5 : 2'bz;  // Controlled_Buffer controlled_buffer_4
  or or_4 (write_enable, decoder_1_out2, decoder_1_out4, decoder_1_out3, decoder_1_out5, decoder_1_out6, decoder_1_out8);
  or or_5 (pcwrite, JUMP, decoder_1_out2, decoder_1_out4, decoder_1_out3, decoder_1_out5, decoder_1_out6, memwrite, decoder_1_out8, decoder_1_out11, decoder_1_out12, decoder_1_out13, decoder_1_out14, decoder_1_out15);
  or or_6 (is_ALU, decoder_1_out2, immediate);
  or or_7 (memread, decoder_1_out8, decoder_1_out7);

  assign dest = in_1[13:10];
  assign out_3 = in_1;
  assign source2 = in_1[5:2];

  // Notes on the sheet:
  //   alu with registers
  //   ADDI
  //   ANDI
  //   ORI
  //   XORI
  //   LD
  //   LD2
  //   ST
  //   JUMP
  //   BEQ
  //   BGT
  //   BLT
  //   BGE
  //   BLE
endmodule

module ALU_Immediate_Control (
  input  addi,
  input  ori,
  input  xori,
  output out_4,
  output out_5
);

  or or_1 (out_5, xori, addi);
  or or_2 (out_4, xori, ori);
endmodule

module CPU (
  input  in_1,
  output [17:0] out_2,
  output [5:0] out_3,
  output [17:0] out_4
);

  wire branch_controller_is_branch_true, clock_1_out, control_unit_1_immediate, control_unit_1_is_alu,
       control_unit_1_is_branch, control_unit_1_jump, control_unit_1_memread, control_unit_1_memwrite,
       control_unit_1_pcwrite, control_unit_1_write_enable;
  wire [1:0] control_unit_1_alu_operate_code_2bit;
  wire [3:0] control_unit_1_dest, control_unit_1_source1, control_unit_1_source2;
  wire [9:0] Program_Counter_output_adress, rom_1_data;
  wire [13:10] rom_1_data_2;
  wire [17:0] ALU_sum, ram_1_data, register_file_1_outdata1, register_file_1_outdata2;
  wire [17:14] rom_1_data_3;

  Clock clock_1 (.out(clock_1_out));
  Program_Counter Program_Counter (
    .adress_of_jump({rom_1_data_2, rom_1_data}), .adress_branch(out_3), .unlock(control_unit_1_pcwrite),
    .set_zero(in_1), ._1_branch___0_1(control_unit_1_is_branch), .jump_or_not(control_unit_1_jump),
    .clock(clock_1_out), .output_adress(Program_Counter_output_adress));
  assign out_3 = branch_controller_is_branch_true ? rom_1_data[5:0] : 6'bz;  // Controlled_Buffer controlled_buffer_1
  ROM #(.addrWidth(10), .dataWidth(18)) rom_1 (
    .addr(Program_Counter_output_adress), .data({rom_1_data_3, rom_1_data_2, rom_1_data}), .sel(1'b1));
  Control_Unit control_unit_1 (
    .in_1({rom_1_data_3, rom_1_data_2, rom_1_data}), .dest(control_unit_1_dest),
    .source1(control_unit_1_source1), .source2(control_unit_1_source2), .clk(clock_1_out), .out_3(out_2),
    .is_ALU(control_unit_1_is_alu), .alu_operate_code_2bit(control_unit_1_alu_operate_code_2bit),
    .immediate(control_unit_1_immediate), .memread(control_unit_1_memread),
    .memwrite(control_unit_1_memwrite), .write_enable(control_unit_1_write_enable),
    .pcwrite(control_unit_1_pcwrite), .JUMP(control_unit_1_jump), .is_Branch(control_unit_1_is_branch));
  Register_File register_file_1 (
    .dr(control_unit_1_dest), .inData(out_4), .sr1(control_unit_1_source1), .sr2(control_unit_1_source2),
    .Write_Enable(control_unit_1_write_enable), .clk(clock_1_out), .outdata1(register_file_1_outdata1),
    .outdata2(register_file_1_outdata2));  // open: out_9, out_10, out_11, out_12, out_13, out_14, out_15, out_16, out_17, out_18, out_19, out_20, out_21, out_22, out_23, out_24
  Arithmetic_Logic_Unit ALU (
    .imm_or_register(control_unit_1_immediate), .input1(register_file_1_outdata1),
    .input2(register_file_1_outdata2), .immediate_value(rom_1_data[5:0]),
    .in_2(control_unit_1_alu_operate_code_2bit), .sum(ALU_sum));
  Multiplexer #(.width(18), .enable("false")) multiplexer_1 (
    .in0(ram_1_data), .in1(ALU_sum), .out(out_4), .sel(control_unit_1_is_alu));
  Branch_Controller branch_controller (
    .opcode_input(rom_1_data_3), .op1(register_file_1_outdata1), .op2(register_file_1_outdata2),
    .is_Branch_True(branch_controller_is_branch_true));
  RAM #(.addrWidth(10), .dataWidth(18), .bus("separate")) ram_1 (
    .addr(rom_1_data), .din(register_file_1_outdata1), .data(ram_1_data), .str(control_unit_1_memwrite),
    .sel(1'b1), .clk(clock_1_out), .ld(control_unit_1_memread), .clr(1'b0));

  // Notes on the sheet:
  //   contents of rom_1 (hex, n*v repeats v):
  //   1c405 1c806 1cc07 1d008 1d409 1d80a 1dc0b a049 e4cc a8d0 ad5b b1e2 2680f 28003 2c4bb 30485 3448f
  //   384b1 3c485
endmodule

module _18_bit_Comparator (
  input  [17:0] op1,
  input  [17:0] op2,
  output greater,
  output less,
  output equal
);

  wire full_comparator_1_eq, full_comparator_1_gt, full_comparator_1_lt, full_comparator_2_eq,
       full_comparator_2_gt, full_comparator_2_lt, full_comparator_3_eq, full_comparator_3_gt,
       full_comparator_3_lt, full_comparator_4_eq, full_comparator_4_gt, full_comparator_4_lt,
       full_comparator_5_eq, full_comparator_5_gt, full_comparator_5_lt, full_comparator_6_eq,
       full_comparator_6_gt, full_comparator_6_lt, full_comparator_7_eq, full_comparator_7_gt,
       full_comparator_7_lt, full_comparator_8_eq, full_comparator_8_gt, full_comparator_8_lt,
       full_comparator_9_eq, full_comparator_9_gt, full_comparator_9_lt, full_comparator_10_eq,
       full_comparator_10_gt, full_comparator_10_lt, full_comparator_11_eq, full_comparator_11_gt,
       full_comparator_11_lt, full_comparator_12_eq, full_comparator_12_gt, full_comparator_12_lt,
       full_comparator_13_eq, full_comparator_13_gt, full_comparator_13_lt, full_comparator_14_eq,
       full_comparator_14_gt, full_comparator_14_lt, full_comparator_15_eq, full_comparator_15_gt,
       full_comparator_15_lt, full_comparator_16_eq, full_comparator_16_gt, full_comparator_16_lt,
       half_comparator_1_eq, half_comparator_1_gt, half_comparator_1_lt;

  Half_Comparator half_comparator_1 (
    .a(op1[17]), .b(op2[17]), .gt(half_comparator_1_gt), .lt(half_comparator_1_lt), .eq(half_comparator_1_eq));
  Full_Comparator full_comparator_1 (
    .gtin(half_comparator_1_gt), .ltin(half_comparator_1_lt), .eqin(half_comparator_1_eq), .a(op1[16]),
    .b(op2[16]), .gt(full_comparator_1_gt), .lt(full_comparator_1_lt), .eq(full_comparator_1_eq));
  Full_Comparator full_comparator_2 (
    .gtin(full_comparator_1_gt), .ltin(full_comparator_1_lt), .eqin(full_comparator_1_eq), .a(op1[15]),
    .b(op2[15]), .gt(full_comparator_2_gt), .lt(full_comparator_2_lt), .eq(full_comparator_2_eq));
  Full_Comparator full_comparator_3 (
    .gtin(full_comparator_2_gt), .ltin(full_comparator_2_lt), .eqin(full_comparator_2_eq), .a(op1[14]),
    .b(op2[14]), .gt(full_comparator_3_gt), .lt(full_comparator_3_lt), .eq(full_comparator_3_eq));
  Full_Comparator full_comparator_4 (
    .gtin(full_comparator_3_gt), .ltin(full_comparator_3_lt), .eqin(full_comparator_3_eq), .a(op1[13]),
    .b(op2[13]), .gt(full_comparator_4_gt), .lt(full_comparator_4_lt), .eq(full_comparator_4_eq));
  Full_Comparator full_comparator_5 (
    .gtin(full_comparator_4_gt), .ltin(full_comparator_4_lt), .eqin(full_comparator_4_eq), .a(op1[12]),
    .b(op2[12]), .gt(full_comparator_5_gt), .lt(full_comparator_5_lt), .eq(full_comparator_5_eq));
  Full_Comparator full_comparator_6 (
    .gtin(full_comparator_5_gt), .ltin(full_comparator_5_lt), .eqin(full_comparator_5_eq), .a(op1[11]),
    .b(op2[11]), .gt(full_comparator_6_gt), .lt(full_comparator_6_lt), .eq(full_comparator_6_eq));
  Full_Comparator full_comparator_7 (
    .gtin(full_comparator_6_gt), .ltin(full_comparator_6_lt), .eqin(full_comparator_6_eq), .a(op1[10]),
    .b(op2[10]), .gt(full_comparator_7_gt), .lt(full_comparator_7_lt), .eq(full_comparator_7_eq));
  Full_Comparator full_comparator_8 (
    .gtin(full_comparator_7_gt), .ltin(full_comparator_7_lt), .eqin(full_comparator_7_eq), .a(op1[9]),
    .b(op2[9]), .gt(full_comparator_8_gt), .lt(full_comparator_8_lt), .eq(full_comparator_8_eq));
  Full_Comparator full_comparator_9 (
    .gtin(full_comparator_8_gt), .ltin(full_comparator_8_lt), .eqin(full_comparator_8_eq), .a(op1[8]),
    .b(op2[8]), .gt(full_comparator_9_gt), .lt(full_comparator_9_lt), .eq(full_comparator_9_eq));
  Full_Comparator full_comparator_10 (
    .gtin(full_comparator_9_gt), .ltin(full_comparator_9_lt), .eqin(full_comparator_9_eq), .a(op1[7]),
    .b(op2[7]), .gt(full_comparator_10_gt), .lt(full_comparator_10_lt), .eq(full_comparator_10_eq));
  Full_Comparator full_comparator_11 (
    .gtin(full_comparator_10_gt), .ltin(full_comparator_10_lt), .eqin(full_comparator_10_eq), .a(op1[6]),
    .b(op2[6]), .gt(full_comparator_11_gt), .lt(full_comparator_11_lt), .eq(full_comparator_11_eq));
  Full_Comparator full_comparator_12 (
    .gtin(full_comparator_11_gt), .ltin(full_comparator_11_lt), .eqin(full_comparator_11_eq), .a(op1[5]),
    .b(op2[5]), .gt(full_comparator_12_gt), .lt(full_comparator_12_lt), .eq(full_comparator_12_eq));
  Full_Comparator full_comparator_13 (
    .gtin(full_comparator_12_gt), .ltin(full_comparator_12_lt), .eqin(full_comparator_12_eq), .a(op1[4]),
    .b(op2[4]), .gt(full_comparator_13_gt), .lt(full_comparator_13_lt), .eq(full_comparator_13_eq));
  Full_Comparator full_comparator_14 (
    .gtin(full_comparator_13_gt), .ltin(full_comparator_13_lt), .eqin(full_comparator_13_eq), .a(op1[3]),
    .b(op2[3]), .gt(full_comparator_14_gt), .lt(full_comparator_14_lt), .eq(full_comparator_14_eq));
  Full_Comparator full_comparator_15 (
    .gtin(full_comparator_14_gt), .ltin(full_comparator_14_lt), .eqin(full_comparator_14_eq), .a(op1[2]),
    .b(op2[2]), .gt(full_comparator_15_gt), .lt(full_comparator_15_lt), .eq(full_comparator_15_eq));
  Full_Comparator full_comparator_16 (
    .gtin(full_comparator_15_gt), .ltin(full_comparator_15_lt), .eqin(full_comparator_15_eq), .a(op1[1]),
    .b(op2[1]), .gt(full_comparator_16_gt), .lt(full_comparator_16_lt), .eq(full_comparator_16_eq));
  Full_Comparator full_comparator_17 (
    .gtin(full_comparator_16_gt), .ltin(full_comparator_16_lt), .eqin(full_comparator_16_eq), .a(op1[0]),
    .b(op2[0]), .gt(greater), .lt(less), .eq(equal));
endmodule

module _10bit_Adder (
  input  [9:0] operand1,
  input  carry_in,
  input  [9:0] operand2,
  output [9:0] \output 
);

  wire full_adder_1_cout, full_adder_2_cout, full_adder_3_cout, full_adder_4_cout, full_adder_5_cout,
       full_adder_6_cout, full_adder_7_cout, full_adder_8_cout, full_adder_9_cout, full_adder_10_cout;

  Full_adder full_adder_1 (.a(operand2[0]), .b(operand1[0]), .cin(carry_in), .s(\output [0]), .cout(full_adder_1_cout));
  Full_adder full_adder_2 (
    .a(operand2[9]), .b(operand1[9]), .cin(full_adder_10_cout), .s(\output [9]), .cout(full_adder_2_cout));
  Full_adder full_adder_3 (
    .a(operand1[1]), .b(operand2[1]), .cin(full_adder_1_cout), .s(\output [1]), .cout(full_adder_3_cout));
  Full_adder full_adder_4 (
    .a(operand1[2]), .b(operand2[2]), .cin(full_adder_3_cout), .s(\output [2]), .cout(full_adder_4_cout));
  Full_adder full_adder_5 (
    .a(operand1[3]), .b(operand2[3]), .cin(full_adder_4_cout), .s(\output [3]), .cout(full_adder_5_cout));
  Full_adder full_adder_6 (
    .a(operand1[4]), .b(operand2[4]), .cin(full_adder_5_cout), .s(\output [4]), .cout(full_adder_6_cout));
  Full_adder full_adder_7 (
    .a(operand1[5]), .b(operand2[5]), .cin(full_adder_6_cout), .s(\output [5]), .cout(full_adder_7_cout));
  Full_adder full_adder_8 (
    .a(operand1[6]), .b(operand2[6]), .cin(full_adder_7_cout), .s(\output [6]), .cout(full_adder_8_cout));
  Full_adder full_adder_9 (
    .a(operand1[7]), .b(operand2[7]), .cin(full_adder_8_cout), .s(\output [7]), .cout(full_adder_9_cout));
  Full_adder full_adder_10 (
    .a(operand1[8]), .b(operand2[8]), .cin(full_adder_9_cout), .s(\output [8]), .cout(full_adder_10_cout));
endmodule

module _2sComplement (
  input  [9:0] in_1,
  output [9:0] \output ,
  output is_negative
);

  wire [9:0] not_1_out;

  not not_1 (not_1_out[0], in_1[0]);
  not not_2 (not_1_out[1], in_1[1]);
  not not_3 (not_1_out[2], in_1[2]);
  not not_4 (not_1_out[3], in_1[3]);
  not not_5 (not_1_out[4], in_1[4]);
  not not_6 (not_1_out[5], in_1[5]);
  not not_7 (not_1_out[6], in_1[6]);
  not not_8 (not_1_out[7], in_1[7]);
  not not_9 (not_1_out[8], in_1[8]);
  not not_10 (not_1_out[9], in_1[9]);
  _10bit_Adder u_10bit_adder_1 (.operand1(not_1_out), .carry_in(1'b0), .operand2(10'h1), .\output (\output ));

  assign is_negative = in_1[9];
endmodule

module Program_Counter (
  input  [13:0] adress_of_jump,
  input  jump_or_not,
  input  _1_branch___0_1,
  input  [5:0] adress_branch,
  input  unlock,
  input  set_zero,
  input  clock,
  output [9:0] output_adress
);

  wire _2s_Complement_2_is_negative, _2s_Complement_is_negative;
  wire [9:0] _2s_Complement_2_output, _2s_Complement_output, address_1_output, address_branch_2_output,
       address_branch_output, bit_extender_1_out, multiplexer_1_out, multiplexer_2_out, multiplexer_3_out,
       multiplexer_4_out, multiplexer_5_out, multiplexer_6_out, subtractor_1_out, subtractor_2_out;

  assign bit_extender_1_out = {{4{adress_branch[5]}}, adress_branch};  // Bit_Extender bit_extender_1
  _2sComplement _2s_Complement (
    .in_1(bit_extender_1_out), .\output (_2s_Complement_output), .is_negative(_2s_Complement_is_negative));
  Multiplexer #(.width(10), .enable("false")) multiplexer_1 (
    .in0(bit_extender_1_out), .in1(_2s_Complement_output), .out(multiplexer_1_out), .sel(adress_branch[5]));
  _2sComplement _2s_Complement_2 (
    .in_1(adress_of_jump[9:0]), .\output (_2s_Complement_2_output), .is_negative(_2s_Complement_2_is_negative));
  _10bit_Adder address_1 (.operand1(output_adress), .carry_in(1'b0), .operand2(10'h1), .\output (address_1_output));
  Subtractor #(.width(10)) subtractor_1 (
    .a(output_adress), .b(multiplexer_1_out), .out(subtractor_1_out));  // open: bin, bout
  Multiplexer #(.width(10), .enable("false")) multiplexer_2 (
    .in0(adress_of_jump[9:0]), .in1(_2s_Complement_2_output), .out(multiplexer_2_out),
    .sel(adress_of_jump[13]));
  _10bit_Adder address_branch (
    .operand1(output_adress), .carry_in(1'b0), .operand2(multiplexer_1_out), .\output (address_branch_output));
  Subtractor #(.width(10)) subtractor_2 (
    .a(output_adress), .b(_2s_Complement_2_output), .out(subtractor_2_out));  // open: bin, bout
  Multiplexer #(.width(10), .enable("false")) multiplexer_3 (
    .in0(address_1_output), .in1(multiplexer_4_out), .out(multiplexer_3_out), .sel(_1_branch___0_1));
  Multiplexer #(.width(10), .enable("false")) multiplexer_4 (
    .in0(address_branch_output), .in1(subtractor_1_out), .out(multiplexer_4_out),
    .sel(_2s_Complement_is_negative));
  _10bit_Adder address_branch_2 (
    .operand1(output_adress), .carry_in(1'b0), .operand2(multiplexer_2_out),
    .\output (address_branch_2_output));
  Multiplexer #(.width(10), .enable("false")) multiplexer_5 (
    .in0(address_branch_2_output), .in1(subtractor_2_out), .out(multiplexer_5_out),
    .sel(_2s_Complement_2_is_negative));
  Multiplexer #(.width(10), .enable("false")) multiplexer_6 (
    .in0(multiplexer_3_out), .in1(multiplexer_5_out), .out(multiplexer_6_out), .sel(jump_or_not));
  Register #(.width(10)) register_1 (
    .D(multiplexer_6_out), .en(unlock), .Q(output_adress), .clk(clock), .clr(set_zero));
endmodule

module Branch_Controller (
  input  [3:0] opcode_input,
  input  [17:0] op1,
  input  [17:0] op2,
  output is_Branch_True
);

  wire _18_bit_comparator_equal, _18_bit_comparator_greater, _18_bit_comparator_less, BEQ_out, BGE_out,
       BGT_out, BLE_out, BLT_out, not_1_out, not_2_out, not_3_out, not_4_out, not_5_out, not_6_out;

  _18_bit_Comparator _18_bit_comparator (
    .op1(op1), .op2(op2), .greater(_18_bit_comparator_greater), .less(_18_bit_comparator_less),
    .equal(_18_bit_comparator_equal));
  not not_1 (not_1_out, _18_bit_comparator_equal);
  not not_2 (not_2_out, _18_bit_comparator_less);
  not not_3 (not_3_out, _18_bit_comparator_greater);
  not not_4 (not_4_out, opcode_input[2]);
  not not_5 (not_5_out, opcode_input[1]);
  not not_6 (not_6_out, opcode_input[0]);
  and BEQ (BEQ_out, opcode_input[3], not_4_out, opcode_input[1], opcode_input[0], _18_bit_comparator_equal, not_2_out, not_3_out);
  and BGT (BGT_out, opcode_input[3], opcode_input[2], not_5_out, not_6_out, _18_bit_comparator_greater, not_2_out, not_1_out);
  and BLT (BLT_out, opcode_input[3], opcode_input[2], not_5_out, opcode_input[0], _18_bit_comparator_less, not_1_out, not_3_out);
  and BGE (BGE_out, opcode_input[3], opcode_input[2], opcode_input[1], not_6_out, _18_bit_comparator_equal, _18_bit_comparator_greater, not_2_out);
  and BLE (BLE_out, opcode_input[3], opcode_input[2], opcode_input[1], opcode_input[0], _18_bit_comparator_less, _18_bit_comparator_equal, not_3_out);
  or or_1 (is_Branch_True, BEQ_out, BGT_out, BLT_out, BGE_out, BLE_out);
endmodule

module Full_adder (
  input  a,
  input  b,
  input  cin,
  output s,
  output cout
);

  wire and_1_out, and_2_out, and_3_out, and_4_out, and_5_out, and_6_out, and_7_out, not_1_out, not_2_out,
       not_3_out;

  not not_1 (not_1_out, a);
  not not_2 (not_2_out, b);
  not not_3 (not_3_out, cin);
  and and_1 (and_1_out, cin, not_1_out, not_2_out);
  and and_2 (and_2_out, not_1_out, b, not_3_out);
  and and_3 (and_3_out, not_3_out, a, not_2_out);
  and and_4 (and_4_out, cin, b, a);
  and and_5 (and_5_out, a, b);
  and and_6 (and_6_out, a, cin);
  and and_7 (and_7_out, b, cin);
  or or_1 (cout, and_5_out, and_6_out, and_7_out);
  or or_2 (s, and_2_out, and_1_out, and_3_out, and_4_out);
endmodule

module Full_Comparator (
  input  gtin,
  input  ltin,
  input  eqin,
  input  a,
  input  b,
  output gt,
  output lt,
  output eq
);

  wire and_1_out, and_2_out, and_3_out, and_4_out, and_5_out, and_6_out, not_1_out, not_2_out, or_1_out;

  not not_1 (not_1_out, a);
  not not_2 (not_2_out, b);
  and and_1 (and_1_out, a, b);
  and and_2 (and_2_out, not_1_out, not_2_out);
  and and_3 (and_3_out, a, not_2_out);
  and and_4 (and_4_out, not_1_out, b);
  and and_5 (and_5_out, eqin, and_3_out);
  or or_1 (or_1_out, and_1_out, and_2_out);
  and and_6 (and_6_out, eqin, and_4_out);
  or or_2 (gt, gtin, and_5_out);
  and and_7 (eq, eqin, or_1_out);
  or or_3 (lt, ltin, and_6_out);
endmodule

module Half_Comparator (
  input  a,
  input  b,
  output gt,
  output lt,
  output eq
);

  wire and_1_out, and_2_out, not_1_out, not_2_out;

  not not_1 (not_1_out, a);
  not not_2 (not_2_out, b);
  and and_1 (and_1_out, a, b);
  and and_2 (and_2_out, not_1_out, not_2_out);
  and and_3 (gt, a, not_2_out);
  and and_4 (lt, not_1_out, b);
  or or_1 (eq, and_1_out, and_2_out);
endmodule
